// Logisim project IT012_Lab01_25520782.circ as structural Verilog: 5 circuits, main circuit Warmup
module Warmup (
  input  A,
  input  B,
  output F
);

  wire not_1_out;

  not not_1 (not_1_out, B);
  and and_1 (F, A, not_1_out);
endmodule

module TN1 (
  input  A,
  input  B,
  input  C,
  output A_prime,
  output AND,
  output OR,
  output NAND,
  output NOR,
  output XOR,
  output XNOR,
  output XOR3,
  output NAND3,
  output CHAIN
);

  wire nand_3_out;

  not not_1 (A_prime, A);
  and and_1 (AND, B, A);
  or or_1 (OR, B, A);
  nand nand_1 (NAND, B, A);
  nor nor_1 (NOR, B, A);
  xor xor_1 (XOR, B, A);
  xnor xnor_1 (XNOR, B, A);
  xor xor_2 (XOR3, C, B, A);
  nand nand_2 (NAND3, C, B, A);
  nand nand_3 (nand_3_out, B, A);
  nand nand_4 (CHAIN, nand_3_out, C);
endmodule

module TN2 (
  input  x,
  input  y,
  input  z,
  output EQ1,
  output EQ2,
  output EQ3,
  output EQ4,
  output EQ5
);

  wire and_1_out, and_2_out, and_3_out, and_4_out, and_5_out, and_6_out, nand_1_out, nor_1_out, not_1_out,
       not_2_out, not_3_out, not_4_out, not_5_out, not_6_out, or_1_out, or_2_out, or_3_out, or_4_out,
       or_5_out, or_6_out;

  nor nor_1 (nor_1_out, y, x);
  not not_1 (not_1_out, y);
  not not_2 (not_2_out, x);
  nand nand_1 (nand_1_out, y, x);
  not not_3 (not_3_out, y);
  not not_4 (not_4_out, x);
  and and_1 (and_1_out, z, y);
  or or_1 (or_1_out, y, x);
  or or_2 (or_2_out, z, x);
  not not_5 (not_5_out, x);
  not not_6 (not_6_out, x);
  and and_2 (and_2_out, not_1_out, not_2_out);
  and and_3 (and_3_out, not_3_out, not_4_out);
  or or_3 (or_3_out, and_1_out, x);
  and and_4 (and_4_out, or_1_out, or_2_out);
  and and_5 (and_5_out, not_5_out, y);
  and and_6 (and_6_out, not_6_out, y);
  or or_4 (or_4_out, and_5_out, x);
  or or_5 (or_5_out, and_6_out, x);
  or or_6 (or_6_out, y, x);
  xnor xnor_1 (EQ1, nor_1_out, and_2_out);
  xnor xnor_2 (EQ2, nand_1_out, and_3_out);
  xnor xnor_3 (EQ3, or_3_out, and_4_out);
  xnor xnor_4 (EQ4, or_4_out, x);
  xnor xnor_5 (EQ5, or_5_out, or_6_out);
endmodule

module TN3 (
  input  A,
  input  B,
  input  C,
  input  D,
  output F
);

  wire and_1_out, and_2_out, and_3_out, and_4_out, and_5_out, and_6_out, not_1_out, not_2_out, not_3_out,
       not_4_out;

  not not_1 (not_1_out, A);
  not not_2 (not_2_out, B);
  not not_3 (not_3_out, C);
  not not_4 (not_4_out, D);
  and and_1 (and_1_out, not_4_out, C, not_2_out, not_1_out);
  and and_2 (and_2_out, D, C, not_2_out, not_1_out);
  and and_3 (and_3_out, D, not_3_out, B, not_1_out);
  and and_4 (and_4_out, D, C, B, not_1_out);
  and and_5 (and_5_out, D, C, not_2_out, A);
  and and_6 (and_6_out, D, not_3_out, B, A);
  or or_1 (F, and_1_out, and_2_out, and_3_out, and_4_out, and_5_out, and_6_out);
endmodule

module TN4 (
  input  A,
  input  B,
  input  C,
  input  D,
  output F_can
);

  wire and_1_out, and_2_out, and_3_out, and_4_out, and_5_out, and_6_out, not_1_out, not_2_out, not_3_out,
       not_4_out;

  not not_1 (not_1_out, A);
  not not_2 (not_2_out, B);
  not not_3 (not_3_out, C);
  not not_4 (not_4_out, D);
  and and_1 (and_1_out, not_4_out, C, not_2_out, not_1_out);
  and and_2 (and_2_out, D, C, not_2_out, not_1_out);
  and and_3 (and_3_out, D, not_3_out, B, not_1_out);
  and and_4 (and_4_out, D, C, B, not_1_out);
  and and_5 (and_5_out, D, C, not_2_out, A);
  and and_6 (and_6_out, D, not_3_out, B, A);
  or or_1 (F_can, and_1_out, and_2_out, and_3_out, and_4_out, and_5_out, and_6_out);
endmodule
